# Fritzing sketch Bluetooth (saved by Fritzing 0.9.3b)

parts:
  Bluetooth = Bluetooth HC-05 Macho
  Arduino_UNO = Arduino Uno (Rev3)

nets:
  N1: Bluetooth.TXD, Arduino_UNO.D4
  N2: Bluetooth.RXD, Arduino_UNO.D5_PWM
  VCC: Bluetooth.VCC, Arduino_UNO.3V3
  GND: Bluetooth.GND, Arduino_UNO.GND
