# Fritzing sketch HC (saved by Fritzing 0.9.3b)
breadboards: 1

parts:
  hc-sr1 = hc-sr04
  Arduino_UNO = Arduino Uno (Rev3)

nets:
  VCC: hc-sr1.VCC, Arduino_UNO.5V
  N1: hc-sr1.Trig, Arduino_UNO.D9_PWM
  N2: hc-sr1.Echo, Arduino_UNO.D10_PWM/SS
  GND: hc-sr1.GND, Arduino_UNO.GND
