# Fritzing sketch Projecte (saved by Fritzing 0.9.3b)
breadboards: 1

parts:
  Bluetooth_Module = Bluetooth HC-05 Macho
  State_Button = Pushbutton [package="[SMD]"]
  LED_Vermell = smd LED [color="Red (633nm)" package="0603 [SMD]"]
  LED_Verd = smd LED [color="Green (555nm)" package="0603 [SMD]"]
  R1 = Resistor [tolerance=±5% resistance=220 package="0603 [SMD]"]
  Servo_Vertical = Basic Servo
  Servo_Horitzontal = Basic Servo
  HC-SR04 = hc-sr04
  RTC_Module = Real Time Clock Module - DS1307 RTC Breakout Board
  Arduino_UNO = Arduino Uno (Rev3)
  R2 = Resistor [tolerance=±5% resistance=220 package="0603 [SMD]"]

nets:
  N1: Bluetooth_Module.TXD, Arduino_UNO.D4
  N2: Bluetooth_Module.RXD, Arduino_UNO.D5_PWM
  VCC: Bluetooth_Module.VCC, Arduino_UNO.3V3
  GND: Bluetooth_Module.GND, State_Button.Pin_1, State_Button.Pin_2, R1.Pin_0, Servo_Vertical.gnd, Servo_Horitzontal.gnd, HC-SR04.GND, RTC_Module.GND, Arduino_UNO.GND, Arduino_UNO.D2, R2.Pin_0
  VCC_2: State_Button.Pin_3, State_Button.Pin_4, Servo_Vertical.vcc, Servo_Horitzontal.vcc, HC-SR04.VCC, RTC_Module.5V, Arduino_UNO.5V
  N3: LED_Vermell.cathode, Arduino_UNO.D12/MISO
  N4: LED_Vermell.anode, R1.Pin_1
  N5: LED_Verd.cathode, Arduino_UNO.D11_PWM/MOSI
  N6: LED_Verd.anode, R2.Pin_1
  N7: Servo_Vertical.pulse, Arduino_UNO.D7
  N8: Servo_Horitzontal.pulse, Arduino_UNO.D6_PWM
  N9: HC-SR04.Trig, Arduino_UNO.D9_PWM
  N10: HC-SR04.Echo, Arduino_UNO.D10_PWM/SS
  N11: RTC_Module.SCL, Arduino_UNO.A5/SCL
  N12: RTC_Module.SDA, Arduino_UNO.A4/SDA
