# Fritzing sketch RTC (saved by Fritzing 0.9.3b)
breadboards: 1

parts:
  UNO1 = Arduino Uno (Rev3)
  Componente1 = Real Time Clock Module - DS1307 RTC Breakout Board

nets:
  N1: UNO1.A4/SDA, Componente1.SDA
  N2: UNO1.A5/SCL, Componente1.SCL
  5V: UNO1.5V, Componente1.5V
  GND: UNO1.GND, Componente1.GND
