# Fritzing sketch Servo (saved by Fritzing 0.9.3b)
breadboards: 1

parts:
  UNO = Arduino Uno (Rev3)
  Servo_Horitzontal = Basic Servo
  Servo_Vertical = Basic Servo

nets:
  N1: UNO.D6_PWM, Servo_Horitzontal.pulse
  N2: UNO.D7, Servo_Vertical.pulse
  VCC: UNO.5V, Servo_Horitzontal.vcc, Servo_Vertical.vcc
  GND: UNO.GND, Servo_Horitzontal.gnd, Servo_Vertical.gnd
